# Fritzing sketch Breadboard (saved by Fritzing 0.9.3b)
breadboards: 1

parts:
  U1 = NodeMCU V1.0
  Bauteil1 = BME280 Breakout  # not connected
  JP1 = Header 8 [package=1x08_smd]

nets:
  N1: U1.D2, JP1.3
  N2: U1.D3, JP1.2
  N3: U1.3V3, JP1.8
  N4: U1.GND, JP1.7
  N5: U1.D5, JP1.5
  N6: U1.D7, JP1.6
  N7: U1.D8, JP1.4

custom parts:
  NodeMCU V1.0: ESP8266 based NodeMCU
